# Fritzing sketch RoboCoop (saved by Fritzing 0.9.2b)
breadboards: 2

parts:
  Q1 = Basic FET P-Channel [package="TO220 [THT]"]
  Q2 = Basic FET P-Channel [package="TO220 [THT]"]
  Q4 = Basic FET N-Channel [package="TO220 [THT]"]
  Q3 = Basic FET N-Channel [package="TO220 [THT]"]
  D1 = Rectifier Diode [part_number=1N4001 package="300 mil [THT]"]
  D2 = Rectifier Diode [part_number=1N4001 package="300 mil [THT]"]
  VCC1 = 4 x AAA Battery Mount
  D3 = Rectifier Diode [part_number=1N4001 package="300 mil [THT]"]
  D4 = Rectifier Diode [part_number=1N4001 package="300 mil [THT]"]
  M1 = DC Motor
  R1 = Resistor [tolerance=±5% resistance=220 package=THT]
  R2 = Trimmer Potentiometer [maximum_resistance=10kΩ package=THT]
  AND = IC, DIP package, 14 pins [chip_label=7408N]
  NANO = Arduino Nano (Rev3.0)
  Q5 = NPN-Transistor [package="TO92 [THT]"]
  L1 = Solenoid
  D5 = Rectifier Diode [part_number=1N4001 package="300 mil [THT]"]
  R3 = Resistor [tolerance=±5% resistance=1k package=THT]
  R4 = Resistor [tolerance=±5% resistance=1k package=THT]
  USER_SW = Pushbutton [package=THT]
  R5 = Resistor [tolerance=±5% resistance=1k package=THT]
  MICRO_SW = Pushbutton [package=THT]
  SET = Pushbutton [package=THT]
  SELECT = Pushbutton [package=THT]
  R6 = Resistor [tolerance=±5% resistance=1k package=THT]
  R7 = Resistor [tolerance=±5% resistance=1k package=THT]
  NOT = IC, DIP package, 14 pins [chip_label=SN74LS04N]
  C1 = Ceramic Capacitor [capacitance=100nF package="100 mil [THT, multilayer]"]
  C2 = Ceramic Capacitor [capacitance=100nF package="100 mil [THT, multilayer]"]
  C3 = Electrolytic Capacitor [capacitance=1µF package="100 mil [THT, electrolytic]"]
  U1 = DS3234 [package=ds3234]
  LCD1 = LCD screen

nets:
  N1: Q1.gate, NOT.pin6
  N2: Q1.drain, Q4.drain, D1.anode, D4.cathode, M1.pin_1, C1.0
  N3: Q1.source, Q2.source, D1.cathode, D2.cathode, VCC1.+, C3.+
  N4: Q2.gate, NOT.pin12
  N5: Q2.drain, Q3.drain, D2.anode, D3.cathode, M1.pin_2, C1.1
  N6: Q4.gate, AND.pin3, NOT.pin13
  N7: Q4.source, Q3.source, VCC1.-, D3.anode, D4.anode, C3.-
  N8: Q3.gate, AND.pin6, NOT.pin5
  5V: R1.Pin_0, R2.leg2, AND.pin14, NANO.5V, USER_SW.leg1, MICRO_SW.leg1, SET.leg1, SELECT.leg1, NOT.pin14, LCD1.VDD
  N9: R1.Pin_1, LCD1.LED+
  GND: R2.leg1, AND.pin7, NANO.GND, Q5.E, R4.Pin_0, R5.Pin_0, R6.Pin_0, R7.Pin_0, NOT.pin7, U1.GND, LCD1.VSS, LCD1.LED-
  N10: R2.wiper, LCD1.V0
  N11: AND.pin1, NANO.D5, NOT.pin1
  N12: AND.pin4, NOT.pin2
  N13: AND.pin5, NANO.D13/SCK
  N14: NANO.D2, SELECT.leg0, R7.Pin_1
  N15: NANO.D3, SET.leg0, R6.Pin_1
  N16: NANO.D6, LCD1.DB5
  N17: NANO.D7, LCD1.DB7
  N18: NANO.D8, LCD1.RS
  N19: NANO.D9, LCD1.R/W
  N20: NANO.D10, LCD1.E
  N21: NANO.D11/MOSI, LCD1.DB4
  N22: NANO.D12/MISO, LCD1.DB6
  N23: NANO.A7, R5.Pin_1, MICRO_SW.leg0
  N24: NANO.A5, U1.SCLK
  N25: NANO.A4, U1.DIN
  N26: NANO.A3, R4.Pin_1, USER_SW.leg0
  N27: NANO.A2, R3.Pin_1
  3V3: NANO.3V3, U1.VCC
  N28: Q5.B, R3.Pin_0
  N29: Q5.C, L1.pin1, D5.anode, C2.0
  7V: L1.pin2, D5.cathode, C2.1
